// Logisim project Input.circ as structural Verilog: 2 circuits, main circuit main
module main (
  input  Clear,
  input  Clock,
  input  [6:0] in_3,
  output [15:0] out_4
);

  wire clock_1_out;
  wire [2:0] counter_1_q;
  wire [6:0] subtractor_1_out;
  wire [15:0] multiplexer_1_out, multiplier_1_out, register_1_q, Total_q;
  wire [15:7] undriven;

  Clock clock_1 (.out(clock_1_out));
  Counter #(.width(3), .max('h7)) counter_1 (
    .Q(counter_1_q), .clk(clock_1_out), .clr(Clear));  // open: load, D, count, carry
  Subtractor #(.width(7)) subtractor_1 (.a(in_3), .b(7'b0110000), .out(subtractor_1_out));  // open: bin, bout
  Multiplexer #(.select(3), .width(16), .enable("false")) multiplexer_1 (
    .in0(16'h2710), .in1(16'h3e8), .in2(16'h64), .in3(16'ha), .in4(16'h1), .out(multiplexer_1_out),
    .sel(counter_1_q));  // open: in5, in6, in7
  Multiplier #(.width(16)) multiplier_1 (
    .a({undriven, subtractor_1_out}), .b(multiplexer_1_out), .out(multiplier_1_out));  // open: cin, cout
  Adder #(.width(16)) adder_1 (.a(multiplier_1_out), .b(register_1_q), .out(out_4));  // open: cin, cout
  Register #(.width(16), .trigger("low")) register_1 (
    .D(Total_q), .en(1'b1), .Q(register_1_q), .clk(clock_1_out));  // open: clr
  Register #(.width(16), .trigger("high")) Total (.D(out_4), .en(1'b1), .Q(Total_q), .clk(clock_1_out), .clr(Clear));
endmodule

module Keyboard (
);

  wire button_1_out, button_2_out, clock_1_out, keyboard_1_avail, not_1_out, t_ff_1_q;
  wire [6:0] keyboard_1_data;

  Clock clock_1 (.out(clock_1_out));
  Keyboard_part keyboard_1 (
    .clk(clock_1_out), .re(t_ff_1_q), .clr(button_2_out), .avail(keyboard_1_avail), .data(keyboard_1_data));
  T_Flip_Flop t_ff_1 (.clk(clock_1_out), .T(button_1_out), .Q(t_ff_1_q), .reset(not_1_out));  // open: Qn, preset, en
  Button button_1 (.out(button_1_out));
  Button button_2 (.out(button_2_out));
  not not_1 (not_1_out, keyboard_1_avail);
  main main_1 (.Clear(button_2_out), .Clock(clock_1_out), .in_3(keyboard_1_data));  // open: out_4

  // Notes on the sheet:
  //   Send
  //   Clear
endmodule
